// Logisim project subtractor.circ as structural Verilog: 3 circuits, main circuit halfsubtractor
module halfsubtractor (
  input  A,
  input  B,
  output S,
  output CO
);

  wire not_1_out;

  not not_1 (not_1_out, A);
  xor xor_1 (S, A, B);
  and and_1 (CO, not_1_out, B);
endmodule

module fullsubtractor (
  input  CI,
  input  A,
  input  B,
  output S,
  output CO
);

  wire halfsubtractor_1_co, halfsubtractor_1_s, halfsubtractor_2_co;

  halfsubtractor halfsubtractor_1 (.A(A), .B(B), .S(halfsubtractor_1_s), .CO(halfsubtractor_1_co));
  halfsubtractor halfsubtractor_2 (.A(CI), .B(halfsubtractor_1_s), .S(S), .CO(halfsubtractor_2_co));
  or or_1 (CO, halfsubtractor_2_co, halfsubtractor_1_co);
endmodule

module adder_subtractor (
  input  N,
  input  AO,
  input  BO,
  input  A1,
  input  B1,
  input  A2,
  input  B2,
  input  A3,
  input  B3,
  output S0,
  output S1,
  output S2,
  output S3,
  output CO
);

  wire fullsubtractor_1_co, fullsubtractor_2_co, fullsubtractor_3_co, xor_1_out, xor_2_out, xor_3_out,
       xor_4_out;

  buf xor_1 (xor_1_out, N);  // XOR_Gate
  xor xor_2 (xor_2_out, B1, N);
  xor xor_3 (xor_3_out, B2, N);
  xor xor_4 (xor_4_out, N, B3);
  fullsubtractor fullsubtractor_1 (.CI(N), .A(AO), .B(xor_1_out), .S(S0), .CO(fullsubtractor_1_co));
  fullsubtractor fullsubtractor_2 (.CI(fullsubtractor_1_co), .A(A1), .B(xor_2_out), .S(S1), .CO(fullsubtractor_2_co));
  fullsubtractor fullsubtractor_3 (.CI(fullsubtractor_2_co), .A(A2), .B(xor_3_out), .S(S2), .CO(fullsubtractor_3_co));
  fullsubtractor fullsubtractor_4 (.CI(fullsubtractor_3_co), .A(A3), .B(xor_4_out), .S(S3), .CO(CO));
endmodule
